// Logisim project ass5.circ as structural Verilog
module Control (
  input  [7:0] in_1,
  output lw,
  output sw,
  output addi,
  output add
);

  and u_lw (lw, ~in_1[7], ~in_1[6]);  // AND_Gate
  and u_sw (sw, ~in_1[7], in_1[6]);  // AND_Gate
  and u_Addi (addi, in_1[7], ~in_1[6]);  // AND_Gate
  and u_Add (add, in_1[6], in_1[7]);
endmodule
